# Fritzing sketch Arduino_Spaceship_Interface (saved by Fritzing 1.0.3b)
breadboards: 1

parts:
  LED1 = smd LED [color="Red (660nm)" package="0805 [SMD]"]
  R2 = Resistor [tolerance=±5% resistance=220 package="1206 [SMD]"]
  S1 = Pushbutton [package="[THT]"]
  LED2 = smd LED [color="Red (660nm)" package="0805 [SMD]"]
  R1 = Resistor [tolerance=±5% resistance=10k package="1206 [SMD]"]
  R4 = Resistor [tolerance=±5% resistance=220 package="1206 [SMD]"]
  Part1 = Arduino Uno (Rev3)
  R3 = Resistor [tolerance=±5% resistance=220 package="1206 [SMD]"]
  LED3 = smd LED [color="Green (565nm)" package="0805 [SMD]"]

nets (from the breadboard view):
  N1: LED1.cathode, R4.Pin_1
  N2: LED1.anode, Part1.D5_PWM
  N3: R2.Pin_0, R1.Pin_0, R4.Pin_0, Part1.GND, R3.Pin_0
  N4: R2.Pin_1, LED3.cathode
  N5: S1.Pin_1, S1.Pin_2, R1.Pin_1, Part1.D2
  N6: S1.Pin_3, S1.Pin_4, Part1.5V
  N7: LED2.cathode, R3.Pin_1
  N8: LED2.anode, Part1.D4
  N9: Part1.D3_PWM, LED3.anode
