# Fritzing sketch Mood_Cue (saved by Fritzing 1.0.3b)
breadboards: 1

parts:
  Part1 = Arduino Uno (Rev3)
  C3 = Electrolytic Capacitor [capacitance=1µF voltage=35V package="100 mil [THT, electrolytic]"]
  R1 = Rotary Potentiometer (Small) [maximum_resistance=10kΩ knob_status=50% power=0.5W package=THT]  # not connected
  J1 = Basic Servo
  C4 = Electrolytic Capacitor [capacitance=1µF voltage=35V package="100 mil [THT, electrolytic]"]

nets:
  N1: Part1.D9_PWM, J1.pulse
  5V: Part1.5V, C3.-, C3.+, J1.vcc, C4.+
  GND: Part1.GND, J1.gnd, C4.-
